# Fritzing sketch CellularTemperatureSensorNode (saved by Fritzing 0.9.3b)

parts:
  U1 = ESP32-38PinWide [part_number=ESP32-38PinWide]
  GSM_SIM_GPSR_SMS_SIM900_SIM1 = SIM800L [package=THT]
  DS1 = DS18B20 1-Wire Temperature Sensor [part_number=DS18B20]

nets:
  N1: U1.3.3, DS1.VDD
  N2: U1.GPIO11, GSM_SIM_GPSR_SMS_SIM900_SIM1.GND
  VIN: U1.VIN, GSM_SIM_GPSR_SMS_SIM900_SIM1.5V
  N3: U1.GPIO4, DS1.DQ
  N4: U1.GPIO16, GSM_SIM_GPSR_SMS_SIM900_SIM1.SIM_TXD
  N5: U1.GPIO17, GSM_SIM_GPSR_SMS_SIM900_SIM1.SIM_RXD
  GND: U1.GND, DS1.GND

custom parts:
  ESP32-38PinWide: Generic 38-Pin ESP32 with wide format (only access to one side of pins on a breadboard) based on Stephen Lilley's HiLetgo ESP-WROOM-32 ESP32 ESP-32S Development Board.
